# Fritzing sketch PoolAndSpray (saved by Fritzing 0.9.3b)

parts:
  U1 = BNC [package=bnc]
  ORP_Circuit1 = ORP Circuit
  Potentiometer = Rotary Potentiometer (Small) [maximum_resistance=100kΩ package=THT]
  8_Channel_Relay1 = 8 Channel Power Relay
  5V = shrouded pin header, 10 pins [form="♂ (shrouded male)"]
  Composant3 = Arduino Ethernet Shield (Rev3)  # not connected
  Composant4 = Arduino Mega ADK (Rev3)
  Squix1 = OLED 0.96" 128x64 I2C SSD1306
  GND = shrouded pin header, 10 pins [form="♂ (shrouded male)"]
  DHT21 = DHT11 Humitidy and Temperature Sensor
  3_3V = shrouded pin header, 10 pins [form="♂ (shrouded male)"]
  DS1_TempSensor = DS18B20 1-Wire Temperature Sensor [part_number=DS18B20]
  2__1______-_+_Out = Camdenboss CTB0158-8 [part_number=CTB0158-8 package=THT]
  R3 = Resistor [tolerance=±5% resistance=4.7k package="0805 [SMD]"]
  OPTOCOUPLEUR_L1521_814_Y = Sharp PC817 [package=THT]
  R4 = Resistor [tolerance=±5% resistance=330 package="0805 [SMD]"]
  RJ45_back = shrouded pin header, 8 pins [form="♂ (shrouded male)"]
  Domino/RJ45_back = shrouded pin header, 8 pins [form="♂ (shrouded male)"]  # not connected
  RJ45_back1 = shrouded pin header, 8 pins [form="♂ (shrouded male)"]
  Domino/RJ45_back_2 = shrouded pin header, 8 pins [form="♂ (shrouded male)"]  # not connected
  R5 = Resistor [tolerance=±5% resistance=4.7k package="0805 [SMD]"]
  +_--_OUT = Camdenboss CTB0158-8 [part_number=CTB0158-8 package=THT]
  +_OUT_-- = Camdenboss CTB0158-3 [part_number=CTB0158-3 package=THT]
  Pression_sensor = BNC [package=bnc]

nets:
  N1: U1.GND, ORP_Circuit1.GND#5
  N2: U1.OUT, ORP_Circuit1.PRB
  N3: ORP_Circuit1.GND#0, GND.pin7
  N4: ORP_Circuit1.TX, Composant4.A9
  N5: ORP_Circuit1.Vcc, 5V.pin9
  VCC: Potentiometer.leg1, 8_Channel_Relay1.VCC, Composant4.5V, DHT21.VDD
  GND: Potentiometer.wiper, Composant4.GND, DHT21.GND
  N6: Potentiometer.leg2, Composant4.A10
  N7: 8_Channel_Relay1.IN1, Composant4.D22
  N8: 8_Channel_Relay1.IN2, Composant4.D23
  N9: 8_Channel_Relay1.IN3, Composant4.D24
  N10: 8_Channel_Relay1.IN4, Composant4.D25
  N11: 8_Channel_Relay1.IN5, Composant4.D26
  N12: 8_Channel_Relay1.IN6, Composant4.D27
  N13: 8_Channel_Relay1.IN7, Composant4.D28
  N14: 8_Channel_Relay1.IN8, Composant4.D29
  N15: 8_Channel_Relay1.GND, GND.pin6
  N16: 8_Channel_Relay1.JD-VCC, 5V.pin10
  N17: 8_Channel_Relay1.COM#25, RJ45_back1.pin1
  N18: 8_Channel_Relay1.NO#26, 8_Channel_Relay1.NO#29, 8_Channel_Relay1.NO#32, RJ45_back1.pin4
  N19: 8_Channel_Relay1.COM#28, RJ45_back1.pin2
  N20: 8_Channel_Relay1.COM#31, RJ45_back1.pin3
  N21: 5V.pin1, DS1_TempSensor.VDD, R5.Pin_1, +_OUT_--.pin1
  N22: 5V.pin5, 2__1______-_+_Out.terminal_5, OPTOCOUPLEUR_L1521_814_Y.Pin_4
  N23: Composant4.A8, DHT21.DATA
  N24: Composant4.D21/SCL, Squix1.SCL
  N25: Composant4.D20/SDA, Squix1.SCA
  N26: Composant4.D33, +_OUT_--.terminal_2
  N27: Composant4.D36, 2__1______-_+_Out.terminal_6
  N28: Composant4.D43, +_--_OUT.terminal_8
  N29: Squix1.VCC, 3_3V.pin1
  N30: Squix1.GND, GND.pin5
  N31: GND.pin4, DS1_TempSensor.GND, +_OUT_--.pin3
  N32: GND.pin10, 2__1______-_+_Out.pin4
  N33: DS1_TempSensor.DQ, R5.Pin_0, +_OUT_--.pin2
  N34: 2__1______-_+_Out.pin1, RJ45_back.pin4
  N35: 2__1______-_+_Out.pin2, RJ45_back.pin3
  N36: 2__1______-_+_Out.terminal_1, R4.Pin_0
  N37: 2__1______-_+_Out.terminal_2, OPTOCOUPLEUR_L1521_814_Y.Pin_1
  N38: 2__1______-_+_Out.terminal_4, R3.Pin_0
  N39: R3.Pin_1, OPTOCOUPLEUR_L1521_814_Y.Pin_3
  N40: OPTOCOUPLEUR_L1521_814_Y.Pin_2, R4.Pin_1
  N41: +_--_OUT.pin6, Pression_sensor.OUT
  N42: +_--_OUT.pin7, Pression_sensor.GND

notes:
  PH METRE detecteur de niveau liquide
  PH METRE BNC mesure ph
  Canne d'aspiration Liquide
  ALIMENTATION FILTRATION + 220v
  +24v
  potager
  pelouse derriere
  pelouse devant

custom parts:
  8 Channel Power Relay: An 8 channel power relay. The module operates at 5V.
  DHT11 Humitidy and Temperature Sensor: DHT11 Humidity and Temperature Sensor
